# Fritzing sketch FireLight (saved by Fritzing 0.9.1b)
breadboards: 1

parts:
  Composant1 = Arduino Uno (Rev3)
  BT1 = Bluetooth HC-06u [package=THT]
  LED1 = RGB LED (com. cathode, rgb) [package="5 mm [THT]"]
  R2 = Resistor [tolerance=±5% resistance=330 package="1206 [SMD]"]
  R3 = Resistor [tolerance=±5% resistance=330 package="1206 [SMD]"]
  R4 = Resistor [tolerance=±5% resistance=330 package="1206 [SMD]"]

nets:
  N1: Composant1.D0/RX, BT1.TXD
  N2: Composant1.D1/TX, BT1.RXD
  N3: Composant1.D3_PWM, R4.Pin_0
  N4: Composant1.D5_PWM, R3.Pin_0
  N5: Composant1.D6_PWM, R2.Pin_0
  3V3: Composant1.3V3, BT1.VCC
  GND: Composant1.GND, BT1.GND, LED1.common_cathode
  N6: LED1.red_anode, R4.Pin_1
  N7: LED1.green_anode, R3.Pin_1
  N8: LED1.blue_anode, R2.Pin_1

custom parts:
  Bluetooth HC-06u: Bluetooth HC-06 - face up, pins down 16.5mm x 37.5mm PCB
